# Fritzing sketch BlinkWithoutDelay (saved by Fritzing 0.9.4)
breadboards: 1

parts:
  Part1 = Adafruit HUZZAH32 ESP32 Feather [part_number="Adafruit #3405"]
  LED1 = RGB LED (com. cathode, rgb) [package="5 mm [THT]"]
  R3 = Resistor [tolerance=±5% resistance=430 package=THT]
  R2 = Resistor [tolerance=±5% resistance=430 package=THT]
  R1 = Resistor [tolerance=±5% resistance=470 package=THT]

nets:
  N1: Part1.GND, LED1.common_cathode
  N2: Part1.IO12_A11, R1.Pin_0
  N3: Part1.IO27_A10, R3.Pin_0
  N4: Part1.IO33_A9, R2.Pin_0
  N5: LED1.red_anode, R1.Pin_1
  N6: LED1.green_anode, R2.Pin_1
  N7: LED1.blue_anode, R3.Pin_1
